// Logisim project regfile.circ as structural Verilog: 1 circuit, main circuit regfile
module regfile (
  input  [4:0] ReadIndex1,
  input  [4:0] ReadIndex2,
  input  [4:0] WriteIndex,
  input  [31:0] WriteData,
  input  RegWEn,
  input  clk,
  output [31:0] ra,
  output [31:0] sp,
  output [31:0] t0,
  output [31:0] t1,
  output [31:0] t2,
  output [31:0] s0,
  output [31:0] s1,
  output [31:0] a0,
  output [31:0] ReadData1,
  output [31:0] ReadData2
);

  wire RegWEn0, RegWEn1, RegWEn2, RegWEn3, RegWEn4, RegWEn5, RegWEn6, RegWEn7, RegWEn8, RegWEn9, RegWEn10,
       RegWEn11, RegWEn12, RegWEn13, RegWEn14, RegWEn15, RegWEn16, RegWEn17, RegWEn18, RegWEn19, RegWEn20,
       RegWEn21, RegWEn22, RegWEn23, RegWEn24, RegWEn25, RegWEn26, RegWEn27, RegWEn28, RegWEn29, RegWEn30,
       RegWEn31;
  wire [31:0] x0_in, x0_out, x1_in, x2_in, x3_in, x3_out, x4_in, x4_out, x5_in, x6_in, x7_in, x8_in, x9_in,
       x10_in, x11_in, x11_out, x12_in, x12_out, x13_in, x13_out, x14_in, x14_out, x15_in, x15_out, x16_in,
       x16_out, x17_in, x17_out, x18_in, x18_out, x19_in, x19_out, x20_in, x20_out, x21_in, x21_out, x22_in,
       x22_out, x23_in, x23_out, x24_in, x24_out, x25_in, x25_out, x26_in, x26_out, x27_in, x27_out, x28_in,
       x28_out, x29_in, x29_out, x30_in, x30_out, x31_in, x31_out;

  Register #(.width(32)) x0 (.D(x0_in), .clk(clk), .Q(x0_out), .clr(1'b1));  // open: en
  Register #(.width(32)) x8 (.D(x8_in), .en(RegWEn8), .clk(clk), .Q(s0));  // open: clr
  Register #(.width(32)) x16 (.D(x16_in), .en(RegWEn16), .clk(clk), .Q(x16_out));  // open: clr
  Register #(.width(32)) x24 (.D(x24_in), .en(RegWEn24), .clk(clk), .Q(x24_out));  // open: clr
  Demultiplexer #(.select(5)) demultiplexer_1 (
    .out0(RegWEn0), .out1(RegWEn1), .out2(RegWEn2), .out3(RegWEn3), .out4(RegWEn4), .out5(RegWEn5),
    .out6(RegWEn6), .out7(RegWEn7), .out8(RegWEn8), .out9(RegWEn9), .out10(RegWEn10), .out11(RegWEn11),
    .out12(RegWEn12), .out13(RegWEn13), .out14(RegWEn14), .out15(RegWEn15), .out16(RegWEn16),
    .out17(RegWEn17), .out18(RegWEn18), .out19(RegWEn19), .out20(RegWEn20), .out21(RegWEn21),
    .out22(RegWEn22), .out23(RegWEn23), .out24(RegWEn24), .out25(RegWEn25), .out26(RegWEn26),
    .out27(RegWEn27), .out28(RegWEn28), .out29(RegWEn29), .out30(RegWEn30), .out31(RegWEn31), .in(RegWEn),
    .sel(WriteIndex));
  Register #(.width(32)) x1 (.D(x1_in), .en(RegWEn1), .clk(clk), .Q(ra));  // open: clr
  Register #(.width(32)) x9 (.D(x9_in), .en(RegWEn9), .clk(clk), .Q(s1));  // open: clr
  Register #(.width(32)) x17 (.D(x17_in), .en(RegWEn17), .clk(clk), .Q(x17_out));  // open: clr
  Register #(.width(32)) x25 (.D(x25_in), .en(RegWEn25), .clk(clk), .Q(x25_out));  // open: clr
  Demultiplexer #(.disabled("Z"), .select(5), .width(32)) demultiplexer_2 (
    .out0(x0_in), .out1(x1_in), .out2(x2_in), .out3(x3_in), .out4(x4_in), .out5(x5_in), .out6(x6_in),
    .out7(x7_in), .out8(x8_in), .out9(x9_in), .out10(x10_in), .out11(x11_in), .out12(x12_in), .out13(x13_in),
    .out14(x14_in), .out15(x15_in), .out16(x16_in), .out17(x17_in), .out18(x18_in), .out19(x19_in),
    .out20(x20_in), .out21(x21_in), .out22(x22_in), .out23(x23_in), .out24(x24_in), .out25(x25_in),
    .out26(x26_in), .out27(x27_in), .out28(x28_in), .out29(x29_in), .out30(x30_in), .out31(x31_in),
    .in(WriteData), .sel(WriteIndex));
  Multiplexer #(.disabled("Z"), .select(5), .width(32)) multiplexer_1 (
    .in0(x0_out), .in1(ra), .in2(sp), .in3(x3_out), .in4(x4_out), .in5(t0), .in6(t1), .in7(t2), .in8(s0),
    .in9(s1), .in10(a0), .in11(x11_out), .in12(x12_out), .in13(x13_out), .in14(x14_out), .in15(x15_out),
    .in16(x16_out), .in17(x17_out), .in18(x18_out), .in19(x19_out), .in20(x20_out), .in21(x21_out),
    .in22(x22_out), .in23(x23_out), .in24(x24_out), .in25(x25_out), .in26(x26_out), .in27(x27_out),
    .in28(x28_out), .in29(x29_out), .in30(x30_out), .in31(x31_out), .out(ReadData1), .sel(ReadIndex1));
  Register #(.width(32)) x2 (.D(x2_in), .en(RegWEn2), .clk(clk), .Q(sp));  // open: clr
  Register #(.width(32)) x10 (.D(x10_in), .en(RegWEn10), .clk(clk), .Q(a0));  // open: clr
  Register #(.width(32)) x18 (.D(x18_in), .en(RegWEn18), .clk(clk), .Q(x18_out));  // open: clr
  Register #(.width(32)) x26 (.D(x26_in), .en(RegWEn26), .clk(clk), .Q(x26_out));  // open: clr
  Register #(.width(32)) x3 (.D(x3_in), .en(RegWEn3), .clk(clk), .Q(x3_out));  // open: clr
  Register #(.width(32)) x19 (.D(x19_in), .en(RegWEn19), .clk(clk), .Q(x19_out));  // open: clr
  Register #(.width(32)) x11 (.D(x11_in), .en(RegWEn11), .clk(clk), .Q(x11_out));  // open: clr
  Register #(.width(32)) x27 (.D(x27_in), .en(RegWEn27), .clk(clk), .Q(x27_out));  // open: clr
  Multiplexer #(.disabled("Z"), .select(5), .width(32)) multiplexer_2 (
    .in0(x0_out), .in1(ra), .in2(sp), .in3(x3_out), .in4(x4_out), .in5(t0), .in6(t1), .in7(t2), .in8(s0),
    .in9(s1), .in10(a0), .in11(x11_out), .in12(x12_out), .in13(x13_out), .in14(x14_out), .in15(x15_out),
    .in16(x16_out), .in17(x17_out), .in18(x18_out), .in19(x19_out), .in20(x20_out), .in21(x21_out),
    .in22(x22_out), .in23(x23_out), .in24(x24_out), .in25(x25_out), .in26(x26_out), .in27(x27_out),
    .in28(x28_out), .in29(x29_out), .in30(x30_out), .in31(x31_out), .out(ReadData2), .sel(ReadIndex2));
  Register #(.width(32)) x4 (.D(x4_in), .en(RegWEn4), .clk(clk), .Q(x4_out));  // open: clr
  Register #(.width(32)) x12 (.D(x12_in), .en(RegWEn12), .clk(clk), .Q(x12_out));  // open: clr
  Register #(.width(32)) x20 (.D(x20_in), .en(RegWEn20), .clk(clk), .Q(x20_out));  // open: clr
  Register #(.width(32)) x28 (.D(x28_in), .en(RegWEn28), .clk(clk), .Q(x28_out));  // open: clr
  Register #(.width(32)) x5 (.D(x5_in), .en(RegWEn5), .clk(clk), .Q(t0));  // open: clr
  Register #(.width(32)) x13 (.D(x13_in), .en(RegWEn13), .clk(clk), .Q(x13_out));  // open: clr
  Register #(.width(32)) x21 (.D(x21_in), .en(RegWEn21), .clk(clk), .Q(x21_out));  // open: clr
  Register #(.width(32)) x29 (.D(x29_in), .en(RegWEn29), .clk(clk), .Q(x29_out));  // open: clr
  Register #(.width(32)) x6 (.D(x6_in), .en(RegWEn6), .clk(clk), .Q(t1));  // open: clr
  Register #(.width(32)) x14 (.D(x14_in), .en(RegWEn14), .clk(clk), .Q(x14_out));  // open: clr
  Register #(.width(32)) x22 (.D(x22_in), .en(RegWEn22), .clk(clk), .Q(x22_out));  // open: clr
  Register #(.width(32)) x30 (.D(x30_in), .en(RegWEn30), .clk(clk), .Q(x30_out));  // open: clr
  Register #(.width(32)) x7 (.D(x7_in), .en(RegWEn7), .clk(clk), .Q(t2));  // open: clr
  Register #(.width(32)) x15 (.D(x15_in), .en(RegWEn15), .clk(clk), .Q(x15_out));  // open: clr
  Register #(.width(32)) x23 (.D(x23_in), .en(RegWEn23), .clk(clk), .Q(x23_out));  // open: clr
  Register #(.width(32)) x31 (.D(x31_in), .en(RegWEn31), .clk(clk), .Q(x31_out));  // open: clr

  // Notes on the sheet:
  //   INPUTS to your circuit
  //   DON'T CHANGE THE LOCATIONS OF THE INPUTS AND OUTPUTS!
  //   These are DEBUG/TEST outputs from your circuit.
  //   OUTPUTS from your circuit
endmodule
